// Logisim project cpu.circ as structural Verilog: 14 circuits, main circuit main
module main (
  input  [31:0] in_1
);

  wire alu_1_alu_ena_2, alu_1_borrow_dec, alu_1_borrow_sub, alu_1_carry_add, alu_1_carry_inc, alu_1_e,
       alu_1_g, button_1_out, clock_1_out, control_unit_1_alu, control_unit_1_call, control_unit_1_in,
       control_unit_1_jg, control_unit_1_jif, control_unit_1_jit, control_unit_1_jump, control_unit_1_lod,
       control_unit_1_mov, control_unit_1_out_7, control_unit_1_pop, control_unit_1_push,
       control_unit_1_ram_load_ena, control_unit_1_ram_store_ena, control_unit_1_reg_ena,
       control_unit_1_reset_2, control_unit_1_rts, control_unit_1_stack_ena, control_unit_1_sto,
       control_unit_1_takt_2, flags_1_jump, \rom_1_übertrag ;
  wire [4:0] control_unit_1_alu_opcode;
  wire [7:0] control_unit_1_argument, control_unit_1_drain, control_unit_1_source;
  wire [15:0] alu_1_alu_result, control_unit_1_alu_ops, control_unit_1_out_6, ram_stack_1_ram_value,
       register_1_a, register_1_b, register_1_reg_value, rom_1_pc;
  wire [31:0] rom_1_befehl;

  Clock clock_1 (.out(clock_1_out));
  Button button_1 (.out(button_1_out));
  Hex_Digit_Display hex_digit_display_1 (.value(rom_1_befehl[31:28]));  // open: dp
  Hex_Digit_Display hex_digit_display_2 (.value(rom_1_befehl[27:24]));  // open: dp
  ROM rom_1 (
    .Adresse(control_unit_1_out_6), .Befehl(rom_1_befehl), .JUMP_3(flags_1_jump), .Takt(clock_1_out),
    .Reset(button_1_out), .\Übertrag (\rom_1_übertrag ), .PC(rom_1_pc), .Stack(ram_stack_1_ram_value),
    .RTS(control_unit_1_rts), .JUMP_2(control_unit_1_call), .JUMP(control_unit_1_jump));
  LED \u_Übertrag  (.in(\rom_1_übertrag ));
  Hex_Digit_Display hex_digit_display_3 (.value(rom_1_befehl[23:20]));  // open: dp
  Hex_Digit_Display hex_digit_display_4 (.value(rom_1_befehl[19:16]));  // open: dp
  Control_Unit control_unit_1 (
    .Befehlsbus(rom_1_befehl), .MOV(control_unit_1_mov), .IN(control_unit_1_in), .STO(control_unit_1_sto),
    .LOD(control_unit_1_lod), .POP(control_unit_1_pop), .ALU(control_unit_1_alu),
    .Argument(control_unit_1_argument), .Source(control_unit_1_source), .Drain(control_unit_1_drain),
    .REG_ENA(control_unit_1_reg_ena), .Takt(clock_1_out), .Takt_2(control_unit_1_takt_2),
    .Reset(button_1_out), .Reset_2(control_unit_1_reset_2), .ALU_OPCODE(control_unit_1_alu_opcode),
    .STACK_ENA(control_unit_1_stack_ena), .RAM_LOAD_ENA(control_unit_1_ram_load_ena),
    .RAM_STORE_ENA(control_unit_1_ram_store_ena), .CALL(control_unit_1_call), .PUSH(control_unit_1_push),
    .ALU_OPS(control_unit_1_alu_ops), .JIT(control_unit_1_jit), .JIF(control_unit_1_jif),
    .out_6(control_unit_1_out_6), .RTS(control_unit_1_rts), .JUMP(control_unit_1_jump),
    .JG(control_unit_1_jg), .out_7(control_unit_1_out_7));  // open: PRN
  Hex_Digit_Display hex_digit_display_5 (.value(rom_1_befehl[11:8]));  // open: dp
  Hex_Digit_Display hex_digit_display_6 (.value(rom_1_befehl[15:12]));  // open: dp
  Hex_Digit_Display hex_digit_display_7 (.value(rom_1_befehl[7:4]));  // open: dp
  Hex_Digit_Display hex_digit_display_8 (.value(rom_1_befehl[3:0]));  // open: dp
  Register register_1 (
    .Arg(control_unit_1_argument), .Source(control_unit_1_source), .Drain(control_unit_1_drain),
    .REG_VALUE(register_1_reg_value), .IN(control_unit_1_in), .REG_ENA(control_unit_1_reg_ena),
    .Takt(control_unit_1_takt_2), .\Löschen (control_unit_1_reset_2), .ALU(alu_1_alu_result),
    .RAM(ram_stack_1_ram_value), .MOV(control_unit_1_mov), .LOAD_RAM(control_unit_1_lod),
    .POP_STACK(control_unit_1_pop), .STORE_RAM(control_unit_1_sto), .PUSH_STACK(control_unit_1_push),
    .ALU_2(control_unit_1_alu), .A(register_1_a), .B(register_1_b), .COMP(control_unit_1_out_7));
  ALU alu_1 (
    .ALU_ENA(control_unit_1_alu), .ALU_OPCODE(control_unit_1_alu_opcode), .A(register_1_a), .B(register_1_b),
    .ALU_RESULT(alu_1_alu_result), .CARRY_ADD(alu_1_carry_add), .BORROW_SUB(alu_1_borrow_sub),
    .CARRY_INC(alu_1_carry_inc), .BORROW_DEC(alu_1_borrow_dec), .ALU_ENA_2(alu_1_alu_ena_2), .G(alu_1_g),
    .E(alu_1_e));
  RAM_Stack ram_stack_1 (
    .STACK_ENA(control_unit_1_stack_ena), .Adresse(control_unit_1_out_6), .Daten(register_1_reg_value),
    .POP(control_unit_1_pop), .CALL(control_unit_1_call), .PUSH(control_unit_1_push),
    .Takt(control_unit_1_takt_2), .RAM_CLEAR(control_unit_1_reset_2),
    .ENA_LOAD_RAM(control_unit_1_ram_load_ena), .ENA_STORE_RAM(control_unit_1_ram_store_ena),
    .RAM_VALUE(ram_stack_1_ram_value), .PC(rom_1_pc), .RTS(control_unit_1_rts));
  Flags flags_1 (
    .Equal(alu_1_e), .ALU_Result(alu_1_alu_result), .Greater(alu_1_g), .CARRY_ADD(alu_1_carry_add),
    .CARRY_INC(alu_1_carry_inc), .BORROW_SUB(alu_1_borrow_sub), .BORROW_DEC(alu_1_borrow_dec),
    .ALU_ENA(alu_1_alu_ena_2), .Argument(control_unit_1_argument), .ALU_OPCODE(control_unit_1_alu_ops),
    .JIT(control_unit_1_jit), .JIF(control_unit_1_jif), .Takt(control_unit_1_takt_2), .JUMP(flags_1_jump),
    .JG_ENA(control_unit_1_jg));  // open: JG

  // Notes on the sheet:
  //   Um das Beispielprogramm auszuführen in den Baustein "ROM" gehen. Dazu nach einem Klick auf den Baustein doppelt auf die Lupe drücken. 
endmodule

module Register (
  input  [15:0] RAM,
  input  [15:0] ALU,
  input  REG_ENA,
  input  [7:0] Arg,
  input  [7:0] Source,
  input  [7:0] Drain,
  input  IN,
  input  MOV,
  input  LOAD_RAM,
  input  POP_STACK,
  input  STORE_RAM,
  input  PUSH_STACK,
  input  ALU_2,
  input  COMP,
  input  \Löschen ,
  input  Takt,
  output [15:0] REG_VALUE,
  output [15:0] A,
  output [15:0] B
);

  wire controlled_buffer_1_out, decoder_1_out0, decoder_1_out1, decoder_1_out2, decoder_1_out3,
       decoder_1_out4, decoder_1_out5, decoder_1_out6, decoder_1_out7, decoder_1_out8, decoder_1_out9,
       decoder_1_out10, decoder_1_out11, decoder_1_out12, decoder_1_out13, decoder_1_out14, decoder_1_out15,
       not_1_out, or_1_out, or_2_out, or_3_out, or_4_out, puffer_1_out_2;
  wire [3:0] multiplexer_1_out, multiplexer_2_out, register_5_q, register_5_q_2, register_5_q_3,
       register_5_q_4;
  wire [15:0] controlled_buffer_2_out, or_5_out, pull_resistor_4_node, R0_2_q, R0_q, R1_2_q, R1_q, R2_2_q,
       R2_q, register_1_q, register_2_q, register_3_q, register_4_q, register_6_q, register_7_q,
       register_8_q, register_9_q, register_10_q;

  or or_1 (or_1_out, STORE_RAM, PUSH_STACK);
  Multiplexer #(.width(4), .enable("false")) multiplexer_1 (
    .in0(Drain[3:0]), .in1(Arg[3:0]), .out(multiplexer_1_out), .sel(or_2_out));
  or or_2 (or_2_out, PUSH_STACK, IN, LOAD_RAM, ALU_2, POP_STACK);
  or or_3 (or_3_out, IN, MOV, controlled_buffer_1_out, LOAD_RAM, POP_STACK);
  assign controlled_buffer_1_out = not_1_out ? ALU_2 : 1'bz;  // Controlled_Buffer controlled_buffer_1
  Pull_Resistor pull_resistor_1 (.node(controlled_buffer_1_out));
  not not_1 (not_1_out, COMP);
  assign controlled_buffer_2_out = IN ? {Source, Drain} : 16'bz;  // Controlled_Buffer controlled_buffer_2
  Pull_Resistor pull_resistor_2 (.node(controlled_buffer_2_out));
  Multiplexer #(.width(4), .enable("false")) multiplexer_2 (
    .in0(Source[3:0]), .in1(Arg[3:0]), .out(multiplexer_2_out), .sel(or_1_out));
  Decoder #(.select(4)) decoder_1 (
    .out0(decoder_1_out0), .out1(decoder_1_out1), .out2(decoder_1_out2), .out3(decoder_1_out3),
    .out4(decoder_1_out4), .out5(decoder_1_out5), .out6(decoder_1_out6), .out7(decoder_1_out7),
    .out8(decoder_1_out8), .out9(decoder_1_out9), .out10(decoder_1_out10), .out11(decoder_1_out11),
    .out12(decoder_1_out12), .out13(decoder_1_out13), .out14(decoder_1_out14), .out15(decoder_1_out15),
    .sel(multiplexer_1_out), .en(or_3_out));
  or or_4 (or_4_out, STORE_RAM, PUSH_STACK, MOV);
  Pull_Resistor pull_resistor_3 (.node(RAM));
  Pull_Resistor pull_resistor_4 (.node(pull_resistor_4_node));
  assign or_5_out = ALU | RAM | pull_resistor_4_node | controlled_buffer_2_out;  // OR_Gate or_5, 16 bits wide
  Pull_Resistor pull_resistor_5 (.node(decoder_1_out0));
  Pull_Resistor pull_resistor_6 (.node(decoder_1_out1));
  Pull_Resistor pull_resistor_7 (.node(decoder_1_out2));
  Pull_Resistor pull_resistor_8 (.node(decoder_1_out3));
  Pull_Resistor pull_resistor_9 (.node(decoder_1_out4));
  Pull_Resistor pull_resistor_10 (.node(decoder_1_out5));
  Pull_Resistor pull_resistor_11 (.node(decoder_1_out6));
  Pull_Resistor pull_resistor_12 (.node(decoder_1_out7));
  Pull_Resistor pull_resistor_13 (.node(decoder_1_out8));
  Pull_Resistor pull_resistor_14 (.node(decoder_1_out9));
  Pull_Resistor pull_resistor_15 (.node(decoder_1_out10));
  Pull_Resistor pull_resistor_16 (.node(decoder_1_out11));
  Pull_Resistor pull_resistor_17 (.node(decoder_1_out12));
  Pull_Resistor pull_resistor_18 (.node(decoder_1_out13));
  Pull_Resistor pull_resistor_19 (.node(decoder_1_out14));
  Pull_Resistor pull_resistor_20 (.node(decoder_1_out15));
  Puffer puffer_1 (.in_1(Takt), .out_2(puffer_1_out_2));
  Pull_Resistor pull_resistor_21 (.node(pull_resistor_4_node));
  Register_part #(.width(16)) R0 (.D(or_5_out), .en(decoder_1_out0), .Q(R0_q), .clk(puffer_1_out_2), .clr(\Löschen ));
  Register_part #(.width(16)) R1 (.D(or_5_out), .en(decoder_1_out1), .Q(R1_q), .clk(puffer_1_out_2), .clr(\Löschen ));
  Register_part #(.width(16)) R2 (.D(or_5_out), .en(decoder_1_out2), .Q(R2_q), .clk(puffer_1_out_2), .clr(\Löschen ));
  Register_part #(.width(16)) register_1 (
    .D(or_5_out), .en(decoder_1_out3), .Q(register_1_q), .clk(puffer_1_out_2), .clr(\Löschen ));
  Register_part #(.width(16)) register_2 (
    .D(or_5_out), .en(decoder_1_out4), .Q(register_2_q), .clk(puffer_1_out_2), .clr(\Löschen ));
  Register_part #(.width(16)) register_3 (
    .D(or_5_out), .en(decoder_1_out5), .Q(register_3_q), .clk(puffer_1_out_2), .clr(\Löschen ));
  Register_part #(.width(16)) register_4 (
    .D(or_5_out), .en(decoder_1_out6), .Q(register_4_q), .clk(puffer_1_out_2), .clr(\Löschen ));
  Register_part #(.width(16)) register_5 (
    .D(or_5_out), .en(decoder_1_out7), .Q({register_5_q_4, register_5_q_3, register_5_q_2, register_5_q}),
    .clk(puffer_1_out_2), .clr(\Löschen ));
  Register_part #(.width(16)) R0_2 (
    .D(or_5_out), .en(decoder_1_out8), .Q(R0_2_q), .clk(puffer_1_out_2), .clr(\Löschen ));
  Register_part #(.width(16)) R1_2 (
    .D(or_5_out), .en(decoder_1_out9), .Q(R1_2_q), .clk(puffer_1_out_2), .clr(\Löschen ));
  Register_part #(.width(16)) R2_2 (
    .D(or_5_out), .en(decoder_1_out10), .Q(R2_2_q), .clk(puffer_1_out_2), .clr(\Löschen ));
  Register_part #(.width(16)) register_6 (
    .D(or_5_out), .en(decoder_1_out11), .Q(register_6_q), .clk(puffer_1_out_2), .clr(\Löschen ));
  Register_part #(.width(16)) register_7 (
    .D(or_5_out), .en(decoder_1_out12), .Q(register_7_q), .clk(puffer_1_out_2), .clr(\Löschen ));
  Register_part #(.width(16)) register_8 (
    .D(or_5_out), .en(decoder_1_out13), .Q(register_8_q), .clk(puffer_1_out_2), .clr(\Löschen ));
  Register_part #(.width(16)) register_9 (
    .D(or_5_out), .en(decoder_1_out14), .Q(register_9_q), .clk(puffer_1_out_2), .clr(\Löschen ));
  Register_part #(.width(16)) register_10 (
    .D(or_5_out), .en(decoder_1_out15), .Q(register_10_q), .clk(puffer_1_out_2), .clr(\Löschen ));
  assign REG_VALUE = REG_ENA ? pull_resistor_4_node : 16'bz;  // Controlled_Buffer controlled_buffer_3
  Pull_Resistor pull_resistor_22 (.node(REG_VALUE));
  Multiplexer #(.select(4), .width(16)) multiplexer_3 (
    .in0(R0_q), .in1(R1_q), .in2(R2_q), .in3(register_1_q), .in4(register_2_q), .in5(register_3_q),
    .in6(register_4_q), .in7({register_5_q_4, register_5_q_3, register_5_q_2, register_5_q}), .in8(R0_2_q),
    .in9(R1_2_q), .in10(R2_2_q), .in11(register_6_q), .in12(register_7_q), .in13(register_8_q),
    .in14(register_9_q), .in15(register_10_q), .out(pull_resistor_4_node), .sel(multiplexer_2_out),
    .en(or_4_out));
  REG_ALU_CNTRL reg_alu_cntrl_1 (
    .in_1(R0_q), .in_2(R1_q), .in_3(R2_q), .in_4(register_1_q), .in_5(register_2_q), .in_6(register_3_q),
    .in_7(register_4_q), .in_8({register_5_q_4, register_5_q_3, register_5_q_2, register_5_q}),
    .CNTRL_B(Drain[3:0]), .CNTRL_A(Source[3:0]), .ALU(ALU_2), .A(A), .B(B), .in_9(R0_2_q), .in_10(R1_2_q),
    .in_11(R2_2_q), .in_12(register_6_q), .in_13(register_7_q), .in_14(register_8_q), .in_15(register_9_q),
    .in_16(register_10_q));
  Hex_Digit_Display hex_digit_display_1 (.value(register_5_q_4));  // open: dp
  Hex_Digit_Display hex_digit_display_2 (.value(register_5_q_3));  // open: dp
  Hex_Digit_Display hex_digit_display_3 (.value(register_5_q_2));  // open: dp
  Hex_Digit_Display hex_digit_display_4 (.value(register_5_q));  // open: dp

  // Notes on the sheet:
  //   Anzahl gefundener Primzahlen 
endmodule

module Control_Unit (
  input  [31:0] Befehlsbus,
  input  Takt,
  input  Reset,
  output [7:0] Drain,
  output [4:0] ALU_OPCODE,
  output [15:0] out_6,
  output out_7,
  output [7:0] Source,
  output [7:0] Argument,
  output [15:0] ALU_OPS,
  output REG_ENA,
  output RAM_LOAD_ENA,
  output RAM_STORE_ENA,
  output STACK_ENA,
  output Takt_2,
  output Reset_2,
  output PUSH,
  output ALU,
  output PRN,
  output CALL,
  output MOV,
  output IN,
  output STO,
  output POP,
  output LOD,
  output JIT,
  output JIF,
  output RTS,
  output JUMP,
  output JG
);

  wire comparator_5_eq;

  Comparator comparator_1 (.a(Befehlsbus[31:24]), .b(8'h1), .eq(MOV));  // open: gt, lt
  Comparator comparator_2 (.a(Befehlsbus[31:24]), .b(8'h2), .eq(IN));  // open: gt, lt
  Comparator comparator_3 (.a(Befehlsbus[31:24]), .b(8'h3), .eq(STO));  // open: gt, lt
  Comparator comparator_4 (.a(Befehlsbus[31:24]), .b(8'h4), .eq(LOD));  // open: gt, lt
  Comparator comparator_5 (.a(Befehlsbus[31:24]), .b(8'h5), .eq(comparator_5_eq));  // open: gt, lt
  Comparator comparator_6 (.a(Befehlsbus[31:24]), .b(8'h6), .eq(POP));  // open: gt, lt
  Comparator comparator_7 (.a(Befehlsbus[31:24]), .b(8'h7));  // open: gt, eq, lt
  Comparator comparator_8 (.a(Befehlsbus[31:24]), .b(8'h8), .eq(PRN));  // open: gt, lt
  Comparator comparator_9 (.a(Befehlsbus[31:24]), .b(8'h9), .eq(CALL));  // open: gt, lt
  Comparator comparator_10 (.a(Befehlsbus[31:24]), .b(8'h1a), .eq(JIT));  // open: gt, lt
  Comparator comparator_11 (.a(Befehlsbus[31:24]), .b(8'h1b), .eq(JIF));  // open: gt, lt
  Comparator comparator_12 (.a(Befehlsbus[31:24]), .b(8'ha), .eq(RTS));  // open: gt, lt
  Comparator comparator_13 (.a(Befehlsbus[31:24]), .b(8'h1c), .eq(JUMP));  // open: gt, lt
  Comparator comparator_14 (.a(Befehlsbus[31:24]), .b(8'h20), .eq(JG));  // open: gt, lt
  ALU_CU alu_cu_1 (
    .Opcode(Befehlsbus[31:24]), .ADD(ALU_OPS[0]), .SUB(ALU_OPS[1]), .INC(ALU_OPS[2]), .DEC(ALU_OPS[3]),
    .COMP(ALU_OPS[4]), .SHIFTL(ALU_OPS[5]), .SHIFTR(ALU_OPS[6]), .ROTL(ALU_OPS[7]), .ROTR(ALU_OPS[8]),
    .AND(ALU_OPS[9]), .OR(ALU_OPS[10]), .NOR(ALU_OPS[11]), .NAND(ALU_OPS[12]), .XOR(ALU_OPS[13]),
    .XNOR(ALU_OPS[14]), .ALU(ALU), .MOD(ALU_OPS[15]));
  or or_1 (REG_ENA, ALU, comparator_5_eq, STO);
  or or_2 (RAM_LOAD_ENA, RTS, LOD, POP);
  or or_3 (RAM_STORE_ENA, STO, CALL, comparator_5_eq);
  or or_4 (STACK_ENA, comparator_5_eq, CALL, POP, RTS);
  or or_5 (PUSH, comparator_5_eq, CALL);

  assign ALU_OPCODE = Befehlsbus[28:24];
  assign Argument = Befehlsbus[23:16];
  assign Drain = Befehlsbus[7:0];
  assign out_6 = Befehlsbus[15:0];
  assign out_7 = ALU_OPS[4];
  assign Reset_2 = Reset;
  assign Source = Befehlsbus[15:8];
  assign Takt_2 = Takt;
endmodule

module ALU (
  input  ALU_ENA,
  input  [4:0] ALU_OPCODE,
  input  [15:0] A,
  input  [15:0] B,
  output [15:0] ALU_RESULT,
  output ALU_ENA_2,
  output CARRY_ADD,
  output CARRY_INC,
  output BORROW_SUB,
  output BORROW_DEC,
  output G,
  output E
);

  wire [4:0] bitadder_1_out, bitadder_2_out;
  wire [15:0] adder_1_out, adder_2_out, and_1_out, bit_extender_1_out, bit_extender_2_out, divider_1_out,
       divider_1_rem, nand_1_out, nor_1_out, or_1_out, shifter_1_out, shifter_2_out, shifter_3_out,
       shifter_4_out, subtractor_1_out, subtractor_2_out, xnor_1_out, xor_1_out;

  Pull_Resistor pull_resistor_1 (.node(B));
  Pull_Resistor pull_resistor_2 (.node(A));
  Adder #(.width(16)) adder_1 (.a(A), .b(B), .out(adder_1_out), .cout(CARRY_ADD));  // open: cin
  Subtractor #(.width(16)) subtractor_1 (.a(A), .b(B), .out(subtractor_1_out), .bout(BORROW_SUB));  // open: bin
  Comparator #(.width(16)) comparator_1 (.a(A), .b(B), .gt(G), .eq(E));  // open: lt
  Shifter #(.width(16)) shifter_1 (.in(A), .\dist (B[3:0]), .out(shifter_1_out));
  Shifter #(.width(16), .shift("lr")) shifter_2 (.in(B), .\dist (B[3:0]), .out(shifter_2_out));
  Shifter #(.width(16), .shift("rl")) shifter_3 (.in(A), .\dist (B[3:0]), .out(shifter_3_out));
  Shifter #(.width(16), .shift("rr")) shifter_4 (.in(A), .\dist (B[3:0]), .out(shifter_4_out));
  BitAdder #(.width(16)) bitadder_1 (.in0(A), .out(bitadder_1_out));
  BitAdder #(.width(16)) bitadder_2 (.in0(B), .out(bitadder_2_out));
  assign and_1_out = A & B;  // AND_Gate and_1, 16 bits wide
  assign or_1_out = A | B;  // OR_Gate or_1, 16 bits wide
  assign nor_1_out = ~(A | B);  // NOR_Gate nor_1, 16 bits wide
  assign nand_1_out = ~(A & B);  // NAND_Gate nand_1, 16 bits wide
  assign xor_1_out = A ^ B;  // XOR_Gate xor_1, 16 bits wide
  assign xnor_1_out = ~(A ^ B);  // XNOR_Gate xnor_1, 16 bits wide
  Divider #(.width(16)) divider_1 (.a(A), .b(B), .out(divider_1_out), .rem(divider_1_rem));  // open: upper
  Pull_Resistor pull_resistor_3 (.node(ALU_RESULT));
  Multiplexer #(.select(5), .width(16)) multiplexer_1 (
    .in11(adder_1_out), .in12(subtractor_1_out), .in13(adder_2_out), .in14(subtractor_2_out),
    .in16(shifter_1_out), .in17(shifter_2_out), .in18(shifter_3_out), .in19(shifter_4_out),
    .in20(bit_extender_1_out), .in21(bit_extender_2_out), .in22(and_1_out), .in23(or_1_out),
    .in24(nor_1_out), .in25(nand_1_out), .in26(xor_1_out), .in27(xnor_1_out), .in31(divider_1_rem),
    .out(ALU_RESULT), .sel(ALU_OPCODE), .en(ALU_ENA));  // open: in0, in1, in2, in3, in4, in5, in6, in7, in8, in9, in10, in15, in28, in29, in30
  Adder #(.width(16)) adder_2 (.a(A), .b(16'h1), .out(adder_2_out), .cout(CARRY_INC));  // open: cin
  Subtractor #(.width(16)) subtractor_2 (.a(A), .b(16'h1), .out(subtractor_2_out), .bout(BORROW_DEC));  // open: bin
  assign bit_extender_1_out = {{11{1'b0}}, bitadder_1_out};  // Bit_Extender bit_extender_1
  assign bit_extender_2_out = {{11{1'b0}}, bitadder_2_out};  // Bit_Extender bit_extender_2

  assign ALU_ENA_2 = ALU_ENA;
endmodule

module RAM_Stack (
  input  [15:0] Adresse,
  input  [15:0] Daten,
  input  [15:0] PC,
  input  POP,
  input  CALL,
  input  PUSH,
  input  Takt,
  input  RAM_CLEAR,
  input  ENA_LOAD_RAM,
  input  ENA_STORE_RAM,
  input  STACK_ENA,
  input  RTS,
  output [15:0] RAM_VALUE
);

  wire or_1_out;
  wire [15:0] inc_1_out_2, multiplexer_1_out, multiplexer_2_out, stackpointer_1_out_7;

  Multiplexer #(.width(16), .enable("false")) multiplexer_1 (
    .in0(Daten), .in1(inc_1_out_2), .out(multiplexer_1_out), .sel(CALL));
  INC inc_1 (.in_1(PC), .out_2(inc_1_out_2));
  StackPointer stackpointer_1 (
    .POP(POP), .CALL(CALL), .PUSH(PUSH), .out_7(stackpointer_1_out_7), .Takt(Takt), .Clear(RAM_CLEAR),
    .RTS(RTS));
  Multiplexer #(.width(16), .enable("false")) multiplexer_2 (
    .in0(Adresse), .in1(stackpointer_1_out_7), .out(multiplexer_2_out), .sel(STACK_ENA));
  or or_1 (or_1_out, STACK_ENA, ENA_STORE_RAM, ENA_LOAD_RAM);
  Pull_Resistor pull_resistor_1 (.node(RAM_VALUE));
  RAM #(.addrWidth(16), .dataWidth(16), .bus("separate")) ram_1 (
    .addr(multiplexer_2_out), .din(multiplexer_1_out), .data(RAM_VALUE), .str(ENA_STORE_RAM), .sel(or_1_out),
    .clk(Takt), .ld(ENA_LOAD_RAM), .clr(RAM_CLEAR));

  // Notes on the sheet:
  //   RAM/Stack
endmodule

module Flags (
  input  JG_ENA,
  input  Equal,
  input  [15:0] ALU_Result,
  input  Greater,
  input  CARRY_ADD,
  input  CARRY_INC,
  input  BORROW_SUB,
  input  BORROW_DEC,
  input  ALU_ENA,
  input  Takt,
  input  JIT,
  input  JIF,
  input  [15:0] ALU_OPCODE,
  input  [7:0] Argument,
  output JG,
  output JUMP
);

  wire and_1_out, and_2_out, and_3_out, and_4_out, and_5_out, and_6_out, and_7_out, and_8_out, and_9_out,
       and_10_out, and_11_out, and_12_out, and_14_out, and_15_out, and_16_out, and_17_out, and_18_out,
       and_19_out, and_20_out, Borrow_q, Borrow_qn, Carry_q, Carry_qn, comparator_1_eq, comparator_1_gt,
       comparator_2_eq, controlled_buffer_1_out, controlled_buffer_4_out, controlled_buffer_6_out,
       controlled_buffer_7_out, Equal_q, Equal_qn, Greater_q, Greater_qn, multiplexer_1_out,
       multiplexer_2_out, or_1_out, or_2_out, pull_resistor_2_node, pull_resistor_3_node,
       pull_resistor_5_node, pull_resistor_8_node, SF_q, ZF_q;

  Comparator #(.width(16)) comparator_1 (
    .a(ALU_Result), .b({16{1'b0}}), .gt(comparator_1_gt), .eq(comparator_1_eq));  // open: lt
  and and_1 (and_1_out, ALU_ENA, CARRY_ADD);
  and and_2 (and_2_out, ALU_ENA, CARRY_INC);
  and and_3 (and_3_out, ALU_ENA, BORROW_SUB);
  and and_4 (and_4_out, ALU_ENA, BORROW_DEC);
  Comparator #(.width(16)) comparator_2 (.a({16{1'b0}}), .b(ALU_Result), .eq(comparator_2_eq));  // open: gt, lt
  and and_5 (and_5_out, and_1_out, ALU_OPCODE[0]);
  or or_1 (or_1_out, and_5_out, and_6_out);
  and and_6 (and_6_out, and_2_out, ALU_OPCODE[2]);
  and and_7 (and_7_out, and_3_out, ALU_OPCODE[1]);
  or or_2 (or_2_out, and_7_out, and_8_out);
  and and_8 (and_8_out, and_4_out, ALU_OPCODE[3]);
  and and_9 (and_9_out, ALU_ENA, ALU_OPCODE[4]);
  Multiplexer #(.enable("false")) multiplexer_1 (
    .in0(comparator_1_eq), .in1(Equal), .out(multiplexer_1_out), .sel(and_9_out));
  Multiplexer #(.enable("false")) multiplexer_2 (
    .in0(comparator_1_gt), .in1(Greater), .out(multiplexer_2_out), .sel(and_9_out));
  and and_10 (and_10_out, ALU_ENA, Takt);
  D_Flip_Flop_part ZF (.clk(and_10_out), .D(comparator_2_eq), .Q(ZF_q));  // open: Qn, preset, en, reset
  D_Flip_Flop_part SF (.clk(and_10_out), .D(ALU_Result[15]), .Q(SF_q));  // open: Qn, preset, en, reset
  D_Flip_Flop_part u_Equal (
    .clk(and_10_out), .D(multiplexer_1_out), .Q(Equal_q), .Qn(Equal_qn));  // open: preset, en, reset
  D_Flip_Flop_part u_Greater (
    .clk(and_10_out), .D(multiplexer_2_out), .Q(Greater_q), .Qn(Greater_qn));  // open: preset, en, reset
  D_Flip_Flop_part Carry (.clk(and_10_out), .D(or_1_out), .Q(Carry_q), .Qn(Carry_qn));  // open: preset, en, reset
  D_Flip_Flop_part Borrow (.clk(and_10_out), .D(or_2_out), .Q(Borrow_q), .Qn(Borrow_qn));  // open: preset, en, reset
  and and_11 (and_11_out, Argument[3], Borrow_qn);
  assign controlled_buffer_1_out = JIF ? and_11_out : 1'bz;  // Controlled_Buffer controlled_buffer_1
  Pull_Resistor pull_resistor_1 (.node(controlled_buffer_1_out));
  and and_12 (and_12_out, ~ZF_q, ~SF_q);  // AND_Gate
  and and_13 (JG, and_12_out, JG_ENA);
  and and_14 (and_14_out, Argument[2], Carry_q);
  and and_15 (and_15_out, Argument[2], Carry_qn);
  and and_16 (and_16_out, Argument[3], Borrow_q);
  Pull_Resistor pull_resistor_2 (.node(pull_resistor_2_node));
  assign pull_resistor_2_node = JIT ? and_14_out : 1'bz;  // Controlled_Buffer controlled_buffer_2
  Pull_Resistor pull_resistor_3 (.node(pull_resistor_3_node));
  assign pull_resistor_3_node = JIT ? and_16_out : 1'bz;  // Controlled_Buffer controlled_buffer_3
  assign controlled_buffer_4_out = JIF ? and_15_out : 1'bz;  // Controlled_Buffer controlled_buffer_4
  Pull_Resistor pull_resistor_4 (.node(controlled_buffer_4_out));
  and and_17 (and_17_out, Argument[1], Greater_qn);
  and and_18 (and_18_out, Argument[1], Greater_q);
  and and_19 (and_19_out, Argument[0], Equal_qn);
  Pull_Resistor pull_resistor_5 (.node(pull_resistor_5_node));
  assign pull_resistor_5_node = JIT ? and_18_out : 1'bz;  // Controlled_Buffer controlled_buffer_5
  assign controlled_buffer_6_out = JIF ? and_19_out : 1'bz;  // Controlled_Buffer controlled_buffer_6
  assign controlled_buffer_7_out = JIF ? and_17_out : 1'bz;  // Controlled_Buffer controlled_buffer_7
  Pull_Resistor pull_resistor_6 (.node(controlled_buffer_7_out));
  Pull_Resistor pull_resistor_7 (.node(controlled_buffer_6_out));
  or or_3 (JUMP, controlled_buffer_1_out, pull_resistor_3_node, controlled_buffer_4_out, pull_resistor_2_node, controlled_buffer_7_out, pull_resistor_5_node, controlled_buffer_6_out, pull_resistor_8_node);
  and and_20 (and_20_out, Argument[0], Equal_q);
  Pull_Resistor pull_resistor_8 (.node(pull_resistor_8_node));
  assign pull_resistor_8_node = JIT ? and_20_out : 1'bz;  // Controlled_Buffer controlled_buffer_8
endmodule

module RegisterEinheit (
  input  [15:0] Daten,
  input  \Löschen ,
  input  Takt,
  input  ENA,
  output [15:0] out_5
);

  wire controlled_buffer_1_out, nand_1_out, nand_3_out, nand_4_out, nand_5_out, nand_6_out, nand_8_out,
       nand_9_out, nand_11_out, nand_12_out, nand_13_out, nand_14_out, nand_16_out, nand_17_out, nand_19_out,
       nand_20_out, nand_21_out, nand_22_out, nand_24_out, nand_25_out, nand_27_out, nand_28_out,
       nand_29_out, nand_30_out, nand_32_out, nand_33_out, nand_35_out, nand_36_out, nand_37_out,
       nand_38_out, nand_40_out, nand_41_out, nand_43_out, nand_44_out, nand_45_out, nand_46_out,
       nand_48_out, nand_49_out, nand_51_out, nand_52_out, nand_53_out, nand_54_out, nand_56_out,
       nand_57_out, nand_59_out, nand_60_out, nand_61_out, nand_62_out, nand_64_out, not_1_out, not_2_out,
       not_3_out, not_4_out, not_5_out, not_6_out, not_7_out, not_8_out, not_9_out, not_10_out, not_11_out,
       not_12_out, not_13_out, not_14_out, not_15_out, not_16_out, or_1_out;
  wire [15:0] multiplexer_1_out;

  or or_1 (or_1_out, ENA, \Löschen );
  Multiplexer #(.width(16), .enable("false")) multiplexer_1 (
    .in0(Daten), .in1({16{1'b0}}), .out(multiplexer_1_out), .sel(\Löschen ));
  assign controlled_buffer_1_out = or_1_out ? Takt : 1'bz;  // Controlled_Buffer controlled_buffer_1
  Pull_Resistor pull_resistor_1 (.node(controlled_buffer_1_out));
  not not_1 (not_1_out, multiplexer_1_out[0]);
  nand nand_1 (nand_1_out, multiplexer_1_out[0], controlled_buffer_1_out);
  nand nand_2 (out_5[0], nand_1_out, nand_3_out);
  nand nand_3 (nand_3_out, out_5[0], nand_4_out);
  nand nand_4 (nand_4_out, controlled_buffer_1_out, not_1_out);
  nand nand_5 (nand_5_out, multiplexer_1_out[1], controlled_buffer_1_out);
  not not_2 (not_2_out, multiplexer_1_out[1]);
  nand nand_6 (nand_6_out, controlled_buffer_1_out, not_2_out);
  nand nand_7 (out_5[1], nand_5_out, nand_8_out);
  not not_3 (not_3_out, multiplexer_1_out[2]);
  nand nand_8 (nand_8_out, out_5[1], nand_6_out);
  nand nand_9 (nand_9_out, multiplexer_1_out[2], controlled_buffer_1_out);
  nand nand_10 (out_5[2], nand_9_out, nand_11_out);
  nand nand_11 (nand_11_out, out_5[2], nand_12_out);
  nand nand_12 (nand_12_out, controlled_buffer_1_out, not_3_out);
  nand nand_13 (nand_13_out, multiplexer_1_out[3], controlled_buffer_1_out);
  not not_4 (not_4_out, multiplexer_1_out[3]);
  nand nand_14 (nand_14_out, controlled_buffer_1_out, not_4_out);
  nand nand_15 (out_5[3], nand_13_out, nand_16_out);
  not not_5 (not_5_out, multiplexer_1_out[4]);
  nand nand_16 (nand_16_out, out_5[3], nand_14_out);
  nand nand_17 (nand_17_out, multiplexer_1_out[4], controlled_buffer_1_out);
  nand nand_18 (out_5[4], nand_17_out, nand_19_out);
  nand nand_19 (nand_19_out, out_5[4], nand_20_out);
  nand nand_20 (nand_20_out, controlled_buffer_1_out, not_5_out);
  nand nand_21 (nand_21_out, multiplexer_1_out[5], controlled_buffer_1_out);
  not not_6 (not_6_out, multiplexer_1_out[5]);
  nand nand_22 (nand_22_out, controlled_buffer_1_out, not_6_out);
  nand nand_23 (out_5[5], nand_21_out, nand_24_out);
  not not_7 (not_7_out, multiplexer_1_out[6]);
  nand nand_24 (nand_24_out, out_5[5], nand_22_out);
  nand nand_25 (nand_25_out, multiplexer_1_out[6], controlled_buffer_1_out);
  nand nand_26 (out_5[6], nand_25_out, nand_27_out);
  nand nand_27 (nand_27_out, out_5[6], nand_28_out);
  nand nand_28 (nand_28_out, controlled_buffer_1_out, not_7_out);
  nand nand_29 (nand_29_out, multiplexer_1_out[7], controlled_buffer_1_out);
  not not_8 (not_8_out, multiplexer_1_out[7]);
  nand nand_30 (nand_30_out, controlled_buffer_1_out, not_8_out);
  nand nand_31 (out_5[7], nand_29_out, nand_32_out);
  not not_9 (not_9_out, multiplexer_1_out[8]);
  nand nand_32 (nand_32_out, out_5[7], nand_30_out);
  nand nand_33 (nand_33_out, multiplexer_1_out[8], controlled_buffer_1_out);
  nand nand_34 (out_5[8], nand_33_out, nand_35_out);
  nand nand_35 (nand_35_out, out_5[8], nand_36_out);
  nand nand_36 (nand_36_out, controlled_buffer_1_out, not_9_out);
  nand nand_37 (nand_37_out, multiplexer_1_out[9], controlled_buffer_1_out);
  not not_10 (not_10_out, multiplexer_1_out[9]);
  nand nand_38 (nand_38_out, controlled_buffer_1_out, not_10_out);
  nand nand_39 (out_5[9], nand_37_out, nand_40_out);
  not not_11 (not_11_out, multiplexer_1_out[10]);
  nand nand_40 (nand_40_out, out_5[9], nand_38_out);
  nand nand_41 (nand_41_out, multiplexer_1_out[10], controlled_buffer_1_out);
  nand nand_42 (out_5[10], nand_41_out, nand_43_out);
  nand nand_43 (nand_43_out, out_5[10], nand_44_out);
  nand nand_44 (nand_44_out, controlled_buffer_1_out, not_11_out);
  nand nand_45 (nand_45_out, multiplexer_1_out[11], controlled_buffer_1_out);
  not not_12 (not_12_out, multiplexer_1_out[11]);
  nand nand_46 (nand_46_out, controlled_buffer_1_out, not_12_out);
  nand nand_47 (out_5[11], nand_45_out, nand_48_out);
  not not_13 (not_13_out, multiplexer_1_out[12]);
  nand nand_48 (nand_48_out, out_5[11], nand_46_out);
  nand nand_49 (nand_49_out, multiplexer_1_out[12], controlled_buffer_1_out);
  nand nand_50 (out_5[12], nand_49_out, nand_51_out);
  nand nand_51 (nand_51_out, out_5[12], nand_52_out);
  nand nand_52 (nand_52_out, controlled_buffer_1_out, not_13_out);
  nand nand_53 (nand_53_out, multiplexer_1_out[13], controlled_buffer_1_out);
  not not_14 (not_14_out, multiplexer_1_out[13]);
  nand nand_54 (nand_54_out, controlled_buffer_1_out, not_14_out);
  nand nand_55 (out_5[13], nand_53_out, nand_56_out);
  not not_15 (not_15_out, multiplexer_1_out[14]);
  nand nand_56 (nand_56_out, out_5[13], nand_54_out);
  nand nand_57 (nand_57_out, multiplexer_1_out[14], controlled_buffer_1_out);
  nand nand_58 (out_5[14], nand_57_out, nand_59_out);
  nand nand_59 (nand_59_out, out_5[14], nand_60_out);
  nand nand_60 (nand_60_out, controlled_buffer_1_out, not_15_out);
  nand nand_61 (nand_61_out, multiplexer_1_out[15], controlled_buffer_1_out);
  not not_16 (not_16_out, multiplexer_1_out[15]);
  nand nand_62 (nand_62_out, controlled_buffer_1_out, not_16_out);
  nand nand_63 (out_5[15], nand_61_out, nand_64_out);
  nand nand_64 (nand_64_out, out_5[15], nand_62_out);
endmodule

module StackPointer (
  input  Clear,
  input  Takt,
  input  POP,
  input  CALL,
  input  PUSH,
  input  RTS,
  output [15:0] out_7
);

  wire or_1_out, or_2_out, or_3_out;
  wire [15:0] adder_1_out, controlled_buffer_1_out, or_4_out, pull_resistor_2_node, subtractor_1_out;

  or or_1 (or_1_out, or_2_out, or_3_out);
  or or_2 (or_2_out, POP, RTS);
  or or_3 (or_3_out, CALL, PUSH);
  Register_part #(.width(16)) register_1 (.D(or_4_out), .en(or_1_out), .Q(out_7), .clk(Takt), .clr(Clear));
  assign or_4_out = controlled_buffer_1_out | pull_resistor_2_node;  // OR_Gate or_4, 16 bits wide
  Adder #(.width(16)) adder_1 (.a(out_7), .b(16'h1), .out(adder_1_out));  // open: cin, cout
  Subtractor #(.width(16)) subtractor_1 (.a(out_7), .b(16'h1), .out(subtractor_1_out));  // open: bin, bout
  assign controlled_buffer_1_out = or_2_out ? subtractor_1_out : 16'bz;  // Controlled_Buffer controlled_buffer_1
  Pull_Resistor pull_resistor_1 (.node(controlled_buffer_1_out));
  Pull_Resistor pull_resistor_2 (.node(pull_resistor_2_node));
  assign pull_resistor_2_node = or_3_out ? adder_1_out : 16'bz;  // Controlled_Buffer controlled_buffer_2
endmodule

module Puffer (
  input  in_1,
  output out_2
);

  wire buffer_1_out, buffer_2_out, buffer_3_out, buffer_4_out, buffer_5_out, buffer_6_out, buffer_7_out,
       buffer_8_out, buffer_9_out, buffer_10_out, buffer_11_out, buffer_12_out, buffer_13_out, buffer_14_out,
       buffer_15_out, buffer_16_out, buffer_17_out, buffer_18_out, buffer_19_out, buffer_20_out,
       buffer_21_out, buffer_22_out, buffer_23_out, buffer_24_out, buffer_25_out, buffer_26_out,
       buffer_27_out, buffer_28_out, buffer_29_out, buffer_30_out, buffer_31_out, buffer_32_out,
       buffer_33_out, buffer_34_out, buffer_35_out, buffer_36_out, buffer_37_out, buffer_38_out,
       buffer_39_out, buffer_40_out, buffer_41_out, buffer_42_out, buffer_43_out, buffer_44_out,
       buffer_45_out, buffer_46_out, buffer_47_out;

  buf buffer_1 (buffer_1_out, in_1);
  buf buffer_2 (buffer_2_out, buffer_3_out);
  buf buffer_3 (buffer_3_out, buffer_1_out);
  buf buffer_4 (buffer_4_out, buffer_2_out);
  buf buffer_5 (buffer_5_out, buffer_37_out);
  buf buffer_6 (buffer_6_out, buffer_8_out);
  buf buffer_7 (buffer_7_out, buffer_6_out);
  buf buffer_8 (buffer_8_out, buffer_5_out);
  buf buffer_9 (buffer_9_out, buffer_10_out);
  buf buffer_10 (buffer_10_out, buffer_12_out);
  buf buffer_11 (buffer_11_out, buffer_9_out);
  buf buffer_12 (buffer_12_out, buffer_43_out);
  buf buffer_13 (buffer_13_out, buffer_15_out);
  buf buffer_14 (buffer_14_out, buffer_4_out);
  buf buffer_15 (buffer_15_out, buffer_16_out);
  buf buffer_16 (buffer_16_out, buffer_14_out);
  buf buffer_17 (buffer_17_out, buffer_19_out);
  buf buffer_18 (buffer_18_out, buffer_7_out);
  buf buffer_19 (buffer_19_out, buffer_20_out);
  buf buffer_20 (buffer_20_out, buffer_18_out);
  buf buffer_21 (buffer_21_out, buffer_24_out);
  buf buffer_22 (buffer_22_out, buffer_11_out);
  buf buffer_23 (buffer_23_out, buffer_21_out);
  buf buffer_24 (buffer_24_out, buffer_22_out);
  buf buffer_25 (buffer_25_out, buffer_13_out);
  buf buffer_26 (buffer_26_out, buffer_27_out);
  buf buffer_27 (buffer_27_out, buffer_28_out);
  buf buffer_28 (buffer_28_out, buffer_25_out);
  buf buffer_29 (buffer_29_out, buffer_32_out);
  buf buffer_30 (buffer_30_out, buffer_17_out);
  buf buffer_31 (buffer_31_out, buffer_30_out);
  buf buffer_32 (buffer_32_out, buffer_31_out);
  buf buffer_33 (buffer_33_out, buffer_34_out);
  buf buffer_34 (buffer_34_out, buffer_36_out);
  buf buffer_35 (buffer_35_out, buffer_33_out);
  buf buffer_36 (buffer_36_out, buffer_23_out);
  buf buffer_37 (buffer_37_out, buffer_39_out);
  buf buffer_38 (buffer_38_out, buffer_40_out);
  buf buffer_39 (buffer_39_out, buffer_38_out);
  buf buffer_40 (buffer_40_out, buffer_26_out);
  buf buffer_41 (buffer_41_out, buffer_42_out);
  buf buffer_42 (buffer_42_out, buffer_44_out);
  buf buffer_43 (buffer_43_out, buffer_41_out);
  buf buffer_44 (buffer_44_out, buffer_29_out);
  buf buffer_45 (buffer_45_out, buffer_35_out);
  buf buffer_46 (buffer_46_out, buffer_47_out);
  buf buffer_47 (buffer_47_out, buffer_45_out);
  buf buffer_48 (out_2, buffer_46_out);

  // Notes on the sheet:
  //   Wird zum Speichertiming benutzt
endmodule

module REG_ALU_CNTRL (
  input  [15:0] in_1,
  input  [15:0] in_2,
  input  [15:0] in_3,
  input  [15:0] in_4,
  input  [15:0] in_5,
  input  [15:0] in_6,
  input  [15:0] in_7,
  input  [15:0] in_8,
  input  [15:0] in_9,
  input  [15:0] in_10,
  input  [15:0] in_11,
  input  [15:0] in_12,
  input  [15:0] in_13,
  input  [15:0] in_14,
  input  [15:0] in_15,
  input  [15:0] in_16,
  input  [3:0] CNTRL_B,
  input  [3:0] CNTRL_A,
  input  ALU,
  output [15:0] B,
  output [15:0] A
);

  Multiplexer #(.select(4), .width(16)) multiplexer_1 (
    .in0(in_1), .in1(in_2), .in2(in_3), .in3(in_4), .in4(in_5), .in5(in_6), .in6(in_7), .in7(in_8),
    .in8(in_9), .in9(in_10), .in10(in_11), .in11(in_12), .in12(in_13), .in13(in_14), .in14(in_15),
    .in15(in_16), .out(B), .sel(CNTRL_B), .en(ALU));
  Pull_Resistor pull_resistor_1 (.node(B));
  Multiplexer #(.select(4), .width(16)) multiplexer_2 (
    .in0(in_1), .in1(in_2), .in2(in_3), .in3(in_4), .in4(in_5), .in5(in_6), .in6(in_7), .in7(in_8),
    .in8(in_9), .in9(in_10), .in10(in_11), .in11(in_12), .in12(in_13), .in13(in_14), .in14(in_15),
    .in15(in_16), .out(A), .sel(CNTRL_A), .en(ALU));
  Pull_Resistor pull_resistor_2 (.node(A));
endmodule

module ALU_CU (
  input  [7:0] Opcode,
  output ALU,
  output ADD,
  output SUB,
  output INC,
  output DEC,
  output COMP,
  output SHIFTL,
  output SHIFTR,
  output ROTL,
  output ROTR,
  output AND,
  output OR,
  output NOR,
  output NAND,
  output XOR,
  output XNOR,
  output MOD
);

  Comparator comparator_1 (.a(Opcode), .b(8'hb), .eq(ADD));  // open: gt, lt
  Comparator comparator_2 (.a(Opcode), .b(8'hc), .eq(SUB));  // open: gt, lt
  Comparator comparator_3 (.a(Opcode), .b(8'hd), .eq(INC));  // open: gt, lt
  Comparator comparator_4 (.a(Opcode), .b(8'he), .eq(DEC));  // open: gt, lt
  Comparator comparator_5 (.a(Opcode), .b(8'hf), .eq(COMP));  // open: gt, lt
  Comparator comparator_6 (.a(Opcode), .b(8'h10), .eq(SHIFTL));  // open: gt, lt
  Comparator comparator_7 (.a(Opcode), .b(8'h11), .eq(SHIFTR));  // open: gt, lt
  Comparator comparator_8 (.a(Opcode), .b(8'h12), .eq(ROTL));  // open: gt, lt
  Comparator comparator_9 (.a(Opcode), .b(8'h13), .eq(ROTR));  // open: gt, lt
  Comparator comparator_10 (.a(Opcode), .b(8'h14), .eq(AND));  // open: gt, lt
  Comparator comparator_11 (.a(Opcode), .b(8'h15), .eq(OR));  // open: gt, lt
  Comparator comparator_12 (.a(Opcode), .b(8'h16), .eq(NOR));  // open: gt, lt
  Comparator comparator_13 (.a(Opcode), .b(8'h17), .eq(NAND));  // open: gt, lt
  Comparator comparator_14 (.a(Opcode), .b(8'h18), .eq(XOR));  // open: gt, lt
  Comparator comparator_15 (.a(Opcode), .b(8'h19), .eq(XNOR));  // open: gt, lt
  Comparator comparator_16 (.a(Opcode), .b(8'h1f), .eq(MOD));  // open: gt, lt
  or or_1 (ALU, ADD, SUB, INC, DEC, COMP, SHIFTL, SHIFTR, ROTL, MOD, ROTR, AND, OR, NOR, NAND, XOR, XNOR);
endmodule

module ROM (
  input  JUMP,
  input  JUMP_2,
  input  JUMP_3,
  input  [15:0] Adresse,
  input  [15:0] Stack,
  input  RTS,
  input  Takt,
  input  Reset,
  output [15:0] PC,
  output [31:0] Befehl,
  output \Übertrag 
);

  wire not_1_out, or_1_out, puffer_1_out_2;
  wire [15:0] multiplexer_1_out;

  Multiplexer #(.width(16), .enable("false")) multiplexer_1 (
    .in0(Adresse), .in1(Stack), .out(multiplexer_1_out), .sel(RTS));
  or or_1 (or_1_out, RTS, JUMP_2, JUMP_3, JUMP);
  Counter #(.width(16), .max('hffff)) u_PC (
    .load(or_1_out), .D(multiplexer_1_out), .count(not_1_out), .Q(PC), .carry(\Übertrag ),
    .clk(puffer_1_out_2), .clr(Reset));
  not not_1 (not_1_out, or_1_out);
  Puffer puffer_1 (.in_1(Takt), .out_2(puffer_1_out_2));
  ROM_part #(.addrWidth(16), .dataWidth(32)) rom_1 (.addr(PC), .data(Befehl));  // open: sel

  // Notes on the sheet:
  //   Programm mit Strg+K starten
  //   Datei primzahlentest.hex auswählen und bestätigen.
  //   Rechtsklick auf den Speicherbaustein und "Speicherabbild laden" drücken.
  //   Auf das Register mit Aufschrift PC klicken und mit Adresse 0x000C laden. Dazu Taste C drücken
  //   Programm dauert zu lange zum Beenden ... Die Zählvariable wird in Register R7 gehalten.
  //   contents of rom_1 (hex, n*v repeats v):
  //   2080002 f000800 1a03000a 1f090008 f000905 1b010008 1000503 1c00000b d080800 1c000001 1000603 a000000
  //   0 2060001 2040002 2010001 2027fff f000102 1a02001a 1000100 9000000 f000305 1a010018 d070700 b010104
  //   1c000011
endmodule

module INC (
  input  [15:0] in_1,
  output [15:0] out_2
);

  Adder #(.width(16)) adder_1 (.a(in_1), .b(16'h1), .out(out_2));  // open: cin, cout
endmodule

module D_Flip_Flop (
  input  E,
  input  Takt,
  input  Takt_2,
  input  E1,
  input  E2,
  input  E3,
  input  E4,
  output Q,
  output Q1,
  output Q2,
  output Q3,
  output Q4
);

  wire nand_1_out, nand_2_out, nand_4_out, nand_5_out, nand_6_out, nand_7_out, nand_8_out, nand_9_out,
       nand_10_out, nand_11_out, nand_12_out, nand_14_out, nand_16_out, nand_18_out, nand_20_out, not_1_out,
       not_2_out, not_3_out, not_4_out, not_5_out;

  not not_1 (not_1_out, E);
  nand nand_1 (nand_1_out, E, Takt);
  nand nand_2 (nand_2_out, Takt, not_1_out);
  nand nand_3 (Q, nand_1_out, nand_4_out);
  nand nand_4 (nand_4_out, Q, nand_2_out);
  not not_2 (not_2_out, E1);
  not not_3 (not_3_out, E2);
  not not_4 (not_4_out, E3);
  not not_5 (not_5_out, E4);
  nand nand_5 (nand_5_out, E1, Takt_2);
  nand nand_6 (nand_6_out, Takt_2, not_2_out);
  nand nand_7 (nand_7_out, E2, Takt_2);
  nand nand_8 (nand_8_out, Takt_2, not_3_out);
  nand nand_9 (nand_9_out, E3, Takt_2);
  nand nand_10 (nand_10_out, Takt_2, not_4_out);
  nand nand_11 (nand_11_out, E4, Takt_2);
  nand nand_12 (nand_12_out, Takt_2, not_5_out);
  nand nand_13 (Q1, nand_5_out, nand_14_out);
  nand nand_14 (nand_14_out, Q1, nand_6_out);
  nand nand_15 (Q2, nand_7_out, nand_16_out);
  nand nand_16 (nand_16_out, Q2, nand_8_out);
  nand nand_17 (Q3, nand_9_out, nand_18_out);
  nand nand_18 (nand_18_out, Q3, nand_10_out);
  nand nand_19 (Q4, nand_11_out, nand_20_out);
  nand nand_20 (nand_20_out, Q4, nand_12_out);
endmodule
